// Logisim project Task-3-using-NAND-gate.circ as structural Verilog: 2 circuits, main circuit main
module main (
  input  A,
  input  B,
  input  C,
  output AC_BC_prime
);

  wire nand7400_1_out_9, nand7400_1_out_10, nand7400_1_out_11, nand7400_1_out_12, nand7400_2_out_12;

  NAND7400 nand7400_1 (
    .in_1(nand7400_1_out_11), .in_2(nand7400_1_out_11), .in_3(C), .in_4(C), .in_5(nand7400_1_out_12),
    .in_6(nand7400_1_out_12), .in_7(C), .in_8(A), .out_9(nand7400_1_out_9), .out_10(nand7400_1_out_10),
    .out_11(nand7400_1_out_11), .out_12(nand7400_1_out_12));
  NAND7400 nand7400_2 (
    .in_1(nand7400_1_out_9), .in_2(nand7400_2_out_12), .in_7(B), .in_8(nand7400_1_out_10),
    .out_9(AC_BC_prime), .out_12(nand7400_2_out_12));  // open: in_3, in_4, in_5, in_6, out_10, out_11

  // Notes on the sheet:
  //   C
  //   A
  //   C
  //   B
  //   AC
  //   (AC)'
  //   (BC')'
endmodule

module NAND7400 (
  input  in_1,
  input  in_2,
  input  in_3,
  input  in_4,
  input  in_5,
  input  in_6,
  input  in_7,
  input  in_8,
  output out_9,
  output out_10,
  output out_11,
  output out_12
);

  nand nand_1 (out_9, in_1, in_2);
  nand nand_2 (out_10, in_3, in_4);
  nand nand_3 (out_11, in_5, in_6);
  nand nand_4 (out_12, in_7, in_8);
endmodule
