// Logisim project Task1.circ as structural Verilog: 1 circuit, main circuit main
module main (
  input  A,
  input  A_2,
  input  A_3,
  input  A_4,
  input  B,
  input  B_2,
  input  A_5,
  input  A_6,
  input  B_3,
  input  B_4,
  output A_A__prime__A_prime,
  output A_A__prime__A_prime_2,
  output AB,
  output AB_2,
  output A_B,
  output A_B_2
);

  wire nand_1_out, nand_3_out, nand_4_out, nor_2_out, nor_3_out, nor_4_out;

  nand nand_1 (nand_1_out, A_4, B);
  nand nand_2 (A_A__prime__A_prime, A, A);
  nand nand_3 (nand_3_out, A_5, A_5);
  nand nand_4 (nand_4_out, B_4, B_4);
  nand nand_5 (AB, nand_1_out, nand_1_out);
  nand nand_6 (A_B, nand_3_out, nand_4_out);
  nor nor_1 (A_A__prime__A_prime_2, A_2, A_2);
  nor nor_2 (nor_2_out, A_3, A_3);
  nor nor_3 (nor_3_out, B_2, B_2);
  nor nor_4 (nor_4_out, A_6, B_3);
  nor nor_5 (AB_2, nor_2_out, nor_3_out);
  nor nor_6 (A_B_2, nor_4_out, nor_4_out);

  // Notes on the sheet:
  //   Implementing NOT gate using NAND gate
  //   (A.B)'
  //   Implementing AND gate using NAND gate
  //   Implementing OR gate using NAND gate
  //   A'
  //   B'
  //   Implementing NOT gate using NOR gate
  //   Implementing ANd gate using NOR gate
  //   (A+A)' =A'
  //   (B+B)' =B'
  //   (A+B)'
  //   Implementing OR gate using NOR gate
endmodule
