// Logisim project Task3-using-Nor-Gate.circ as structural Verilog: 2 circuits, main circuit main
module main (
  input  A,
  input  B,
  input  C,
  output out_4
);

  wire nor7402_1_out_9, nor7402_1_out_10, nor7402_1_out_11, nor7402_1_out_12, nor7402_2_out_10,
       nor7402_2_out_12;

  NOR7402 nor7402_1 (
    .in_1(B), .in_2(B), .in_3(nor7402_1_out_11), .in_4(nor7402_1_out_12), .in_5(A), .in_6(A), .in_7(C),
    .in_8(C), .out_9(nor7402_1_out_9), .out_10(nor7402_1_out_10), .out_11(nor7402_1_out_11),
    .out_12(nor7402_1_out_12));
  NOR7402 nor7402_2 (
    .in_1(nor7402_2_out_10), .in_2(nor7402_2_out_10), .in_3(nor7402_1_out_10), .in_4(nor7402_2_out_12),
    .in_7(C), .in_8(nor7402_1_out_9), .out_9(out_4), .out_10(nor7402_2_out_10), .out_12(nor7402_2_out_12));  // open: in_5, in_6, out_11
endmodule

module NOR7402 (
  input  in_1,
  input  in_2,
  input  in_3,
  input  in_4,
  input  in_5,
  input  in_6,
  input  in_7,
  input  in_8,
  output out_9,
  output out_10,
  output out_11,
  output out_12
);

  nor nor_1 (out_9, in_1, in_2);
  nor nor_2 (out_10, in_3, in_4);
  nor nor_3 (out_11, in_5, in_6);
  nor nor_4 (out_12, in_7, in_8);
endmodule
