// Logisim project lab8.circ as structural Verilog: 1 circuit, main circuit main
module main (
  input  in_1,
  output out_2,
  output out_3
);

  wire clock_1_out, DB_qn, xor_1_out, xor_2_out;

  xor xor_1 (xor_1_out, out_2, out_3);
  xor xor_2 (xor_2_out, xor_1_out, in_1);
  Clock clock_1 (.out(clock_1_out));
  D_Flip_Flop DA (.clk(clock_1_out), .D(xor_2_out), .Q(out_2));  // open: Qn, preset, en, reset
  D_Flip_Flop DB (.clk(clock_1_out), .D(DB_qn), .Q(out_3), .Qn(DB_qn));  // open: preset, en, reset

  // Notes on the sheet:
  //   B
  //   A
endmodule
