// Logisim project task2.circ as structural Verilog: 1 circuit, main circuit main
module main (
  input  A,
  input  B,
  input  A_2,
  input  B_2,
  input  A_3,
  input  B_3,
  input  A_4,
  input  B_4,
  output out_9,
  output AB__A_B__prime,
  output AB_A_prime_B_prime,
  output AB_A_prime_B_prime_2
);

  wire nand_1_out, nand_2_out, nand_3_out, nand_4_out, nand_5_out, nand_6_out, nand_8_out, nor_1_out,
       nor_2_out, nor_3_out, nor_4_out, nor_5_out, nor_6_out, nor_7_out;

  not nand_1 (nand_1_out, A);  // NAND_Gate
  nor nor_1 (nor_1_out, B_2, B_2);
  not nand_2 (nand_2_out, A_3);  // NAND_Gate
  nor nor_2 (nor_2_out, A_2, A_2);
  nor nor_3 (nor_3_out, A_4, B_4);
  nand nand_3 (nand_3_out, A, nand_1_out);
  nand nand_4 (nand_4_out, nand_1_out, B);
  nand nand_5 (nand_5_out, A_3, nand_2_out);
  nand nand_6 (nand_6_out, nand_2_out, B_3);
  nor nor_4 (nor_4_out, nor_2_out, nor_1_out);
  nor nor_5 (nor_5_out, A_2, B_2);
  nor nor_6 (nor_6_out, A_4, nor_3_out);
  nor nor_7 (nor_7_out, nor_3_out, B_4);
  nand nand_7 (out_9, nand_3_out, nand_4_out);
  nand nand_8 (nand_8_out, nand_5_out, nand_6_out);
  nor nor_8 (AB__A_B__prime, nor_4_out, nor_5_out);
  nor nor_9 (AB_A_prime_B_prime_2, nor_6_out, nor_7_out);
  nand nand_9 (AB_A_prime_B_prime, nand_8_out, nand_8_out);

  // Notes on the sheet:
  //   (AB)'
  //   Implementing XOR using NAND gate
  //   (AB)'
  //   A'
  //   B'
  //   Implementing XOR gate using NOR gate
  //   Implementing XNOR gate using NAND gate
  //   (A+B)'
  //   Implementing XNOR gate using NOR gate
  //   A'+(A.B)
  //   B'+(A.B)
  //   (A(A.B)')'
  //   (B(A.B)')'
  //   AB
  //   (A+B)'
  //   (A+(A+B)' )'
  //   (B+(A+B)') '
  //   ((A'+A.B)(B+A.B))'
endmodule
